// Logisim project cpu.circ as structural Verilog: 1 circuit, main circuit CPU
module CPU (
  input  [31:0] in_1,
  input  PC_Enable,
  input  PC_RST,
  input  CLK,
  output [31:0] s0,
  output [31:0] s1,
  output [31:0] t0,
  output [31:0] t1,
  output [31:0] a0,
  output [31:0] ra,
  output [31:0] sp,
  output [31:0] Output
);

  // Incrementer incrementer_1: pin names not known
  // PC pc_1: pin names not known
  // RegFile regfile_1: pin names not known
  // ALU alu_1: pin names not known
  // memory_main main_1: pin names not known

  // Other names for the same wires on the sheet: fetch_addr[31:0] = Output; INST[31:0] = in_1; pc_en = PC_Enable

  // Notes on the sheet:
  //   NOTE
  //   Please do not modify/replace/move/change/delete/etc input and output pins
  //   These are debug/test outputs from your circuit
endmodule
